# Fritzing sketch Arduino_Uno_Measurement (saved by Fritzing 1.0.2b)
breadboards: 1

parts:
  M1 = Osoyoo SX1278-ra-02
  A2 = DHT22 module
  Bauteil1 = Arduino Uno (Rev3) - ICSP
  Chirp!_Soil_Moisture_Sensor1 = Chirp! Soil Moisture Sensor v2.7.3
  VCC1 = 4 x AAA Battery Mount  # not connected
  ANT1 = Antenna  # not connected

nets:
  GND: M1.GND, A2.GND, Bauteil1.GND, Chirp!_Soil_Moisture_Sensor1.pin_4
  3.3V: M1.3.3V, Bauteil1.3V3
  N1: M1.RST, Bauteil1.D9_PWM
  N2: M1.SCK, Bauteil1.D13/SCK
  N3: M1.MISO, Bauteil1.ICSP_MISO, Bauteil1.D12/MISO
  N4: M1.MOSI, Bauteil1.ICSP_MOSI, Bauteil1.D11_PWM/MOSI
  N5: M1.NSS, Bauteil1.D10_PWM/SS
  VCC: A2.VCC, Bauteil1.5V, Chirp!_Soil_Moisture_Sensor1.Pin_1
  N6: A2.DAT, Bauteil1.D4
  N7: Bauteil1.A2, Chirp!_Soil_Moisture_Sensor1.pin_2

notes:
  5.5V

custom parts:
  Osoyoo SX1278-ra-02: Osoyoo Long Distance wireless transceiver Uart LoRa Module.
  DHT22 module: DHT22 module. Pins GND VCC Data.
